# Fritzing sketch arkaline (saved by Fritzing 0.9.5d)

parts:
  Part1 = Arduino Uno (Rev3) - ICSP
  M1 = DC Motor
  M2 = DC Motor
  M3 = DC Motor
  M4 = DC Motor
  M5 = BTS7960
  M6 = BTS7960
  Boost_Convertor1 = Boost Convertor [part_number=XL6009E1 package=THT]
  BAT1 = Battery Holders [package=lipo-1100mAh]
  M7 = ps2 gamepad [package=THT]

nets:
  5V: Part1.5V, M5.pin7, M6.pin7, M7.3.3V
  GND: Part1.GND, M5.pin8, M6.pin8, Boost_Convertor1.Negative_Output, M7.GND
  N1: Part1.D8, M5.pin4
  N2: Part1.D9_PWM, M5.pin3
  N3: Part1.D10_PWM/SS, M7.ATT
  N4: Part1.D11_PWM/MOSI, M7.CMD
  N5: Part1.D12/MISO, M7.DAT
  N6: Part1.D13/SCK, M7.CLK
  N7: Part1.D1/TX, M6.pin3
  N8: Part1.D2, M6.pin2
  N9: Part1.D3_PWM, M6.pin1
  N10: Part1.D4, M6.pin4
  N11: Part1.D6_PWM, M5.pin2
  N12: Part1.D7, M5.pin1
  N13: Part1.VIN, Boost_Convertor1.Positive_Output
  N14: M1.pin_1, M2.pin_1, M6.pin9
  N15: M1.pin_2, M2.pin_2, M6.pin10
  N16: M3.pin_1, M4.pin_1, M5.pin9
  N17: M3.pin_2, M4.pin_2, M5.pin10
  N18: M5.pin11, M6.pin11, Boost_Convertor1.Positive_Input, BAT1.+
  N19: M5.pin12, M6.pin12, Boost_Convertor1.Negative_Input, BAT1.-

custom parts:
  BTS7960: BTS7960 43A Peak Power H-Bridge PWM Motor Driver
  Boost Convertor: DC to DC boost convertor
  ps2 gamepad: PS2 gamepad. Warning! PCB view is designed for the female connector available from https://www.robotshop.com/en/ps2-connector.html. However there is no mechanical information that I can find so ipcb was generated from a scaled jpg and may well be wrong. Print the footprint out and check it against a real part before ordering boards!

// code stored in the sketch: arkaline.ino


#define PS2_DAT        12      
#define PS2_CMD        11  
#define PS2_SEL        10  
#define PS2_CLK        13  


//#define leftm1     2
//#define leftm2     3
//#define rightm1    4
//#define rightm2    5
//#define left_EN    6
//#define right_EN   7


#include <PS2X_lib.h>
#include "BTS7960.h"


  //analog values read from PS2 joysticks


int speed = 0;


#define pressures   true
//#define pressures   false
#define rumble      true
//#define rumble      false


PS2X ps2x; // create PS2 Controller Class


int error = 0;
byte type = 0;
byte vibrate = 0;



const uint8_t L1_EN = 4;
const uint8_t R1_EN = 1;
const uint8_t L1_PWM = 2;
const uint8_t R1_PWM = 3;


BTS7960 motor1Controller(R1_EN,L1_EN, L1_PWM, R1_PWM);


const uint8_t L2_EN = 8; //problem
const uint8_t R2_EN = 9;
const uint8_t L2_PWM = 6;
const uint8_t R2_PWM = 7;


BTS7960 motor2Controller(R2_EN,L2_EN, L2_PWM, R2_PWM);



void setup() {


  Serial.begin(57600);


  //pinMode(leftm1,  OUTPUT);
  //pinMode(leftm2,  OUTPUT);
  //pinMode(rightm1, OUTPUT);
  //pinMode(rightm2, OUTPUT);
  //pinMode(left_EN, OUTPUT);
  //pinMode(right_EN, OUTPUT);


  //digitalWrite(left_EN, LOW);
  //digitalWrite(right_EN, LOW);


  //delay(300);  //added delay to give wireless ps2 module some time to startup, before configuring it



  //setup pins and settings: GamePad(clock, command, attention, data, Pressures?, Rumble?) check for error
  error = ps2x.config_gamepad(PS2_CLK,PS2_CMD,PS2_SEL,PS2_DAT, true, true);   
                          //(clock, command, attention, data)


 if(error == 0){
  Serial.println("Found Controller, configured successful");
 }
   
 else if(error == 1)
  Serial.println("No controller found, check wiring or reset the Arduino");
   
 else if(error == 2)
  Serial.println("Controller found but not accepting commands");
  
 else if(error == 3)
  Serial.println("Controller refusing to enter Pressures mode, may not support it.");  
 type = ps2x.readType();
 switch(type) {
  case 0:
    break;
  case 1:
    break;
  case 2:
    break;
  }
}


void loop() {
  ps2x.read_gamepad(false, vibrate); //read controller and set large motor to spin at 'vibrate' speed
  
delay(50);
  if(ps2x.Button(PSB_GREEN)){
      Serial.println("first gear");
      speed=100;}
  
  if(ps2x.ButtonPressed(PSB_RED)){             //will be TRUE if button was JUST pressed
      Serial.println("second gear");
      speed=190;}
         
  if(ps2x.ButtonReleased(PSB_BLUE)){            //will be TRUE if button was JUST released
      Serial.println("third gear");
      speed=225; }    
    
  if(ps2x.NewButtonState(PSB_PINK)) {          //will be TRUE if button was JUST pressed OR released
      Serial.println("fourth gear");
      speed=255;}
  //...................................................................


   if(ps2x.Button(PSB_PAD_UP)) {         //will be TRUE as long as button is pressed
    //Serial.println("Up held , ");
    forward(speed);
      }
  else{
   waithere(); 
  } 
   if(ps2x.Button(PSB_PAD_RIGHT)){
    //Serial.println("Right held , ");
    right(speed);
      }
   if(ps2x.Button(PSB_PAD_LEFT)){
    //Serial.println("LEFT held , ");
    left(speed);
      }
   if(ps2x.Button(PSB_PAD_DOWN)){
    //Serial.println("DOWN held , ");
    REV(speed);
      }
      if(ps2x.Button(PSB_L1)){
    //Serial.println("Right sheld , ");
    sright(speed);
      }
   if(ps2x.Button(PSB_R1)){
    //Serial.println("left sheld , ");
    sleft(speed);
      }
  
}


void right(int speed)
{
   Serial.println("forward");
   motor1Controller. Enable(); 
   motor2Controller.Enable(); 
   motor1Controller.TurnLeft(speed);
   motor2Controller.TurnLeft(speed);


}
void left(int speed)
{
   Serial.println("rev");
   motor1Controller. Enable(); 
   motor2Controller.Enable(); 
   motor1Controller. TurnRight(speed);
   motor2Controller. TurnRight(speed);


}
void forward(int speed)
{
   Serial.println("left");
   motor1Controller. Enable(); 
   motor2Controller.Enable(); 
   motor1Controller. TurnLeft(speed);
   motor2Controller. TurnRight(speed);



}
void REV(int speed)
{
   Serial.println("right");
   motor1Controller. Enable(); 
   motor2Controller.Enable(); 
   motor1Controller. TurnRight(speed);
   motor2Controller. TurnLeft(speed);
}
void sright(int speed)
{
  Serial.println("sright");
  motor1Controller. Enable(); 
   motor2Controller.Enable(); 
   motor1Controller. TurnLeft(0);
   motor2Controller. TurnRight(speed);


}
void sleft(int speed)
{
  Serial.println("sleft");
  motor1Controller. Enable(); 
   motor2Controller.Enable(); 
   motor1Controller. TurnLeft(speed);
   motor2Controller. TurnRight(0);


}
void waithere()
{
  //Serial.println("stop");


  digitalWrite(R2_PWM, LOW);
  digitalWrite(L2_PWM, LOW);
  digitalWrite(R1_PWM, LOW);
  digitalWrite(L1_PWM, LOW);
}
